// Logisim project 3015.circ as structural Verilog
module Register_File (
  input  [19:0] Input_Data,
  input  [3:0] Src1,
  input  [3:0] Src2,
  input  [3:0] DST,
  input  Reset,
  input  Load,
  input  Clock,
  output [19:0] SRC1_2,
  output [19:0] SRC2_2
);

  wire and_1_out, and_2_out, and_3_out, and_4_out, and_5_out, and_6_out, and_7_out, and_8_out, and_9_out,
       and_10_out, and_11_out, and_12_out, and_13_out, and_14_out, and_15_out, and_16_out, decoder_1_out0,
       decoder_1_out1, decoder_1_out2, decoder_1_out3, decoder_1_out4, decoder_1_out5, decoder_1_out6,
       decoder_1_out7, decoder_1_out8, decoder_1_out9, decoder_1_out10, decoder_1_out11, decoder_1_out12,
       decoder_1_out13, decoder_1_out14, decoder_1_out15;
  wire [19:0] register_1_q, register_2_q, register_3_q, register_4_q, register_5_q, register_6_q,
       register_7_q, register_8_q, register_9_q, register_10_q, register_11_q, register_12_q, register_13_q,
       register_14_q, register_15_q, register_16_q;

  Decoder #(.select(4)) decoder_1 (
    .out0(decoder_1_out0), .out1(decoder_1_out1), .out2(decoder_1_out2), .out3(decoder_1_out3),
    .out4(decoder_1_out4), .out5(decoder_1_out5), .out6(decoder_1_out6), .out7(decoder_1_out7),
    .out8(decoder_1_out8), .out9(decoder_1_out9), .out10(decoder_1_out10), .out11(decoder_1_out11),
    .out12(decoder_1_out12), .out13(decoder_1_out13), .out14(decoder_1_out14), .out15(decoder_1_out15),
    .sel(DST));  // open: en
  and and_1 (and_1_out, decoder_1_out0, Load);
  and and_2 (and_2_out, decoder_1_out1, Load);
  and and_3 (and_3_out, decoder_1_out2, Load);
  and and_4 (and_4_out, decoder_1_out3, Load);
  and and_5 (and_5_out, decoder_1_out4, Load);
  and and_6 (and_6_out, decoder_1_out5, Load);
  and and_7 (and_7_out, decoder_1_out6, Load);
  and and_8 (and_8_out, decoder_1_out7, Load);
  Register #(.width(20)) register_1 (.D(Input_Data), .en(and_1_out), .Q(register_1_q), .clk(Clock), .clr(Reset));
  Register #(.width(20)) register_2 (.D(Input_Data), .en(and_2_out), .Q(register_2_q), .clk(Clock), .clr(Reset));
  Register #(.width(20)) register_3 (.D(Input_Data), .en(and_3_out), .Q(register_3_q), .clk(Clock), .clr(Reset));
  Register #(.width(20)) register_4 (.D(Input_Data), .en(and_4_out), .Q(register_4_q), .clk(Clock), .clr(Reset));
  Register #(.width(20)) register_5 (.D(Input_Data), .en(and_5_out), .Q(register_5_q), .clk(Clock), .clr(Reset));
  Register #(.width(20)) register_6 (.D(Input_Data), .en(and_6_out), .Q(register_6_q), .clk(Clock), .clr(Reset));
  Register #(.width(20)) register_7 (.D(Input_Data), .en(and_7_out), .Q(register_7_q), .clk(Clock), .clr(Reset));
  Register #(.width(20)) register_8 (.D(Input_Data), .en(and_8_out), .Q(register_8_q), .clk(Clock), .clr(Reset));
  and and_9 (and_9_out, decoder_1_out8, Load);
  and and_10 (and_10_out, decoder_1_out9, Load);
  and and_11 (and_11_out, decoder_1_out10, Load);
  and and_12 (and_12_out, decoder_1_out11, Load);
  and and_13 (and_13_out, decoder_1_out12, Load);
  and and_14 (and_14_out, decoder_1_out13, Load);
  and and_15 (and_15_out, decoder_1_out14, Load);
  and and_16 (and_16_out, decoder_1_out15, Load);
  Register #(.width(20)) register_9 (.D(Input_Data), .en(and_9_out), .Q(register_9_q), .clk(Clock), .clr(Reset));
  Register #(.width(20)) register_10 (.D(Input_Data), .en(and_10_out), .Q(register_10_q), .clk(Clock), .clr(Reset));
  Register #(.width(20)) register_11 (.en(and_11_out), .Q(register_11_q), .clk(Clock), .clr(Reset));  // open: D
  Register #(.width(20)) register_12 (.D(Input_Data), .en(and_12_out), .Q(register_12_q), .clk(Clock), .clr(Reset));
  Register #(.width(20)) register_13 (.D(Input_Data), .en(and_13_out), .Q(register_13_q), .clk(Clock), .clr(Reset));
  Register #(.width(20)) register_14 (.D(Input_Data), .en(and_14_out), .Q(register_14_q), .clk(Clock), .clr(Reset));
  Register #(.width(20)) register_15 (.D(Input_Data), .en(and_15_out), .Q(register_15_q), .clk(Clock), .clr(Reset));
  Register #(.width(20)) register_16 (.D(Input_Data), .en(and_16_out), .Q(register_16_q), .clk(Clock), .clr(Reset));
  Multiplexer #(.select(4), .width(20), .enable("false")) multiplexer_1 (
    .in0(register_1_q), .in1(register_2_q), .in2(register_3_q), .in3(register_4_q), .in4(register_5_q),
    .in5(register_6_q), .in6(register_7_q), .in7(register_8_q), .in8(register_9_q), .in9(register_10_q),
    .in10(register_11_q), .in11(register_12_q), .in12(register_13_q), .in13(register_14_q),
    .in14(register_15_q), .in15(register_16_q), .out(SRC1_2), .sel(Src1));
  Multiplexer #(.select(4), .width(20), .enable("false")) multiplexer_2 (
    .in0(register_1_q), .in1(register_2_q), .in2(register_3_q), .in3(register_4_q), .in4(register_5_q),
    .in5(register_6_q), .in6(register_7_q), .in7(register_8_q), .in8(register_9_q), .in9(register_10_q),
    .in10(register_11_q), .in11(register_12_q), .in12(register_13_q), .in13(register_14_q),
    .in14(register_15_q), .in15(register_16_q), .out(SRC2_2), .sel(Src2));
endmodule

module _20_Bit_Adder (
  input  [19:0] Input1,
  input  [19:0] Input2,
  output [19:0] Sum_Out,
  output C_out
);

  wire Full_Adder_2_c_out, Full_Adder_3_c_out, Full_Adder_4_c_out, Full_Adder_5_c_out, Full_Adder_6_c_out,
       Full_Adder_7_c_out, Full_Adder_8_c_out, Full_Adder_9_c_out, Full_Adder_10_c_out, Full_Adder_11_c_out,
       Full_Adder_12_c_out, Full_Adder_13_c_out, Full_Adder_14_c_out, Full_Adder_15_c_out,
       Full_Adder_16_c_out, Full_Adder_17_c_out, Full_Adder_18_c_out, Full_Adder_c_out, Half_Adder_c_out;

  Half_Adder Half_Adder (.Input_1(Input1[0]), .Input_2(Input2[0]), .Sum(Sum_Out[0]), .C_out(Half_Adder_c_out));
  Full_Adder Full_Adder (
    .C_in(Half_Adder_c_out), .Input_1(Input1[1]), .Input_2(Input2[1]), .Sum(Sum_Out[1]),
    .C_out(Full_Adder_c_out));
  Full_Adder Full_Adder_2 (
    .C_in(Full_Adder_c_out), .Input_1(Input1[2]), .Input_2(Input2[2]), .Sum(Sum_Out[2]),
    .C_out(Full_Adder_2_c_out));
  Full_Adder Full_Adder_3 (
    .C_in(Full_Adder_2_c_out), .Input_1(Input1[3]), .Input_2(Input2[3]), .Sum(Sum_Out[3]),
    .C_out(Full_Adder_3_c_out));
  Full_Adder Full_Adder_4 (
    .C_in(Full_Adder_3_c_out), .Input_1(Input1[4]), .Input_2(Input2[4]), .Sum(Sum_Out[4]),
    .C_out(Full_Adder_4_c_out));
  Full_Adder Full_Adder_5 (
    .C_in(Full_Adder_4_c_out), .Input_1(Input1[5]), .Input_2(Input2[5]), .Sum(Sum_Out[5]),
    .C_out(Full_Adder_5_c_out));
  Full_Adder Full_Adder_6 (
    .C_in(Full_Adder_5_c_out), .Input_1(Input1[6]), .Input_2(Input2[6]), .Sum(Sum_Out[6]),
    .C_out(Full_Adder_6_c_out));
  Full_Adder Full_Adder_7 (
    .C_in(Full_Adder_6_c_out), .Input_1(Input1[7]), .Input_2(Input2[7]), .Sum(Sum_Out[7]),
    .C_out(Full_Adder_7_c_out));
  Full_Adder Full_Adder_8 (
    .C_in(Full_Adder_7_c_out), .Input_1(Input1[8]), .Input_2(Input2[8]), .Sum(Sum_Out[8]),
    .C_out(Full_Adder_8_c_out));
  Full_Adder Full_Adder_9 (
    .C_in(Full_Adder_8_c_out), .Input_1(Input1[9]), .Input_2(Input2[9]), .Sum(Sum_Out[9]),
    .C_out(Full_Adder_9_c_out));
  Full_Adder Full_Adder_10 (
    .C_in(Full_Adder_9_c_out), .Input_1(Input1[10]), .Input_2(Input2[10]), .Sum(Sum_Out[10]),
    .C_out(Full_Adder_10_c_out));
  Full_Adder Full_Adder_11 (
    .C_in(Full_Adder_10_c_out), .Input_1(Input1[11]), .Input_2(Input2[11]), .Sum(Sum_Out[11]),
    .C_out(Full_Adder_11_c_out));
  Full_Adder Full_Adder_12 (
    .C_in(Full_Adder_11_c_out), .Input_1(Input1[12]), .Input_2(Input2[12]), .Sum(Sum_Out[12]),
    .C_out(Full_Adder_12_c_out));
  Full_Adder Full_Adder_13 (
    .C_in(Full_Adder_12_c_out), .Input_1(Input1[13]), .Input_2(Input2[13]), .Sum(Sum_Out[13]),
    .C_out(Full_Adder_13_c_out));
  Full_Adder Full_Adder_14 (
    .C_in(Full_Adder_13_c_out), .Input_1(Input1[14]), .Input_2(Input2[14]), .Sum(Sum_Out[14]),
    .C_out(Full_Adder_14_c_out));
  Full_Adder Full_Adder_15 (
    .C_in(Full_Adder_14_c_out), .Input_1(Input1[15]), .Input_2(Input2[15]), .Sum(Sum_Out[15]),
    .C_out(Full_Adder_15_c_out));
  Full_Adder Full_Adder_16 (
    .C_in(Full_Adder_15_c_out), .Input_1(Input1[16]), .Input_2(Input2[16]), .Sum(Sum_Out[16]),
    .C_out(Full_Adder_16_c_out));
  Full_Adder Full_Adder_17 (
    .C_in(Full_Adder_16_c_out), .Input_1(Input1[17]), .Input_2(Input2[17]), .Sum(Sum_Out[17]),
    .C_out(Full_Adder_17_c_out));
  Full_Adder Full_Adder_18 (
    .C_in(Full_Adder_17_c_out), .Input_1(Input1[18]), .Input_2(Input2[18]), .Sum(Sum_Out[18]),
    .C_out(Full_Adder_18_c_out));
  Full_Adder Full_Adder_19 (
    .C_in(Full_Adder_18_c_out), .Input_1(Input1[19]), .Input_2(Input2[19]), .Sum(Sum_Out[19]), .C_out(C_out));
endmodule

module Full_Adder (
  input  C_in,
  input  Input_1,
  input  Input_2,
  output Sum,
  output C_out
);

  wire and_1_out, and_2_out, and_3_out;

  xor xor_1 (Sum, C_in, Input_1, Input_2);
  and and_1 (and_1_out, C_in, Input_1);
  and and_2 (and_2_out, C_in, Input_2);
  and and_3 (and_3_out, Input_1, Input_2);
  or or_1 (C_out, and_1_out, and_2_out, and_3_out);
endmodule

module Half_Adder (
  input  Input_1,
  input  Input_2,
  output Sum,
  output C_out
);

  xor xor_1 (Sum, Input_1, Input_2);
  and and_1 (C_out, Input_1, Input_2);
endmodule

module Arithmetic_Logic_Unit (
  input  [19:0] SR1,
  input  [19:0] SR2,
  input  [19:0] IMM,
  input  Select,
  input  [3:0] ALU_Select,
  output [19:0] out_6
);

  wire _20BitAdder_c_out;
  wire [19:0] _20BitAdder_sum_out, and_1_out, multiplexer_1_out, or_1_out, xor_1_out;

  Multiplexer #(.width(20), .enable("false")) multiplexer_1 (
    .in0(SR2), .in1(IMM), .out(multiplexer_1_out), .sel(Select));
  _20_Bit_Adder _20BitAdder (
    .Input1(SR1), .Input2(multiplexer_1_out), .Sum_Out(_20BitAdder_sum_out), .C_out(_20BitAdder_c_out));
  assign xor_1_out = SR1 ^ multiplexer_1_out;  // XOR_Gate xor_1, 20 bits wide
  assign or_1_out = SR1 | multiplexer_1_out;  // OR_Gate or_1, 20 bits wide
  assign and_1_out = SR1 & multiplexer_1_out;  // AND_Gate and_1, 20 bits wide
  Multiplexer #(.select(4), .width(20), .enable("false")) multiplexer_2 (
    .in1(_20BitAdder_sum_out), .in2(xor_1_out), .in4(or_1_out), .in7(and_1_out), .out(out_6), .sel(ALU_Select));  // open: in0, in3, in5, in6, in8, in9, in10, in11, in12, in13, in14, in15
  // also tied to GND on the sheet: _20BitAdder_c_out
endmodule

module Instruction_Memory (
  output [17:0] Instruction
);

  wire [17:0] undriven;

  ROM #(.addrWidth(18), .dataWidth(18)) rom_1 (.addr(undriven), .data(Instruction));  // open: sel

  // Notes on the sheet:
  //   contents of rom_1 (hex, n*v repeats v):
  //   0 1c403 4840 10800 c000 2c842 28009 21881 1dc47 2e5f1 11c01
endmodule

module Program_Counter (
  input  [19:0] JmpAddress,
  input  PCWrite,
  input  Reset,
  input  PC_Read,
  input  Clk,
  output CarryOut,
  output [19:0] Out
);

  wire multiplexer_1_out, multiplexer_2_out, multiplexer_3_out, multiplexer_4_out, multiplexer_5_out,
       multiplexer_6_out, multiplexer_7_out, multiplexer_8_out, multiplexer_9_out, multiplexer_10_out,
       multiplexer_11_out, multiplexer_12_out, multiplexer_13_out, multiplexer_14_out, multiplexer_15_out,
       multiplexer_16_out, multiplexer_17_out, multiplexer_18_out;
  wire [19:0] adder_1_out;

  Multiplexer #(.select(2), .enable("false")) multiplexer_1 (
    .in0(adder_1_out[17]), .in1(JmpAddress[17]), .in2(1'b0), .in3(1'b0), .out(multiplexer_1_out),
    .sel({Reset, PCWrite}));
  D_Flip_Flop d_ff_1 (.clk(Clk), .D(multiplexer_1_out), .Q(Out[17]), .en(PC_Read));  // open: Qn, preset, reset
  Multiplexer #(.select(2), .enable("false")) multiplexer_2 (
    .in0(adder_1_out[16]), .in1(JmpAddress[16]), .in2(1'b0), .in3(1'b0), .out(multiplexer_2_out),
    .sel({Reset, PCWrite}));
  D_Flip_Flop d_ff_2 (.clk(Clk), .D(multiplexer_2_out), .Q(Out[16]), .en(PC_Read));  // open: Qn, preset, reset
  Multiplexer #(.select(2), .enable("false")) multiplexer_3 (
    .in0(adder_1_out[15]), .in1(JmpAddress[15]), .in2(1'b0), .in3(1'b0), .out(multiplexer_3_out),
    .sel({Reset, PCWrite}));
  Multiplexer #(.select(2), .enable("false")) multiplexer_4 (
    .in0(adder_1_out[14]), .in1(JmpAddress[14]), .in2(1'b0), .in3(1'b0), .out(multiplexer_4_out),
    .sel({Reset, PCWrite}));
  D_Flip_Flop d_ff_3 (.clk(Clk), .D(multiplexer_3_out), .Q(Out[15]), .en(PC_Read));  // open: Qn, preset, reset
  Multiplexer #(.select(2), .enable("false")) multiplexer_5 (
    .in0(adder_1_out[13]), .in1(JmpAddress[13]), .in2(1'b0), .in3(1'b0), .out(multiplexer_5_out),
    .sel({Reset, PCWrite}));
  D_Flip_Flop d_ff_4 (.clk(Clk), .D(multiplexer_4_out), .Q(Out[14]), .en(PC_Read));  // open: Qn, preset, reset
  D_Flip_Flop d_ff_5 (.D(multiplexer_5_out), .Q(Out[13]), .en(PC_Read));  // open: clk, Qn, preset, reset
  Multiplexer #(.select(2), .enable("false")) multiplexer_6 (
    .in0(adder_1_out[12]), .in1(JmpAddress[12]), .in2(1'b0), .in3(1'b0), .out(multiplexer_6_out),
    .sel({Reset, PCWrite}));
  Multiplexer #(.select(2), .enable("false")) multiplexer_7 (
    .in0(adder_1_out[11]), .in1(JmpAddress[11]), .in2(1'b0), .in3(1'b0), .out(multiplexer_7_out),
    .sel({Reset, PCWrite}));
  D_Flip_Flop d_ff_6 (.clk(Clk), .D(multiplexer_6_out), .Q(Out[12]), .en(PC_Read));  // open: Qn, preset, reset
  D_Flip_Flop d_ff_7 (.clk(Clk), .D(multiplexer_7_out), .Q(Out[11]), .en(PC_Read));  // open: Qn, preset, reset
  Multiplexer #(.select(2), .enable("false")) multiplexer_8 (
    .in0(adder_1_out[10]), .in1(JmpAddress[10]), .in2(1'b0), .in3(1'b0), .out(multiplexer_8_out),
    .sel({Reset, PCWrite}));
  D_Flip_Flop d_ff_8 (.clk(Clk), .D(multiplexer_8_out), .Q(Out[10]), .en(PC_Read));  // open: Qn, preset, reset
  Multiplexer #(.select(2), .enable("false")) multiplexer_9 (
    .in0(adder_1_out[9]), .in1(JmpAddress[9]), .in2(1'b0), .in3(1'b0), .out(multiplexer_9_out),
    .sel({Reset, PCWrite}));
  Multiplexer #(.select(2), .enable("false")) multiplexer_10 (
    .in0(adder_1_out[8]), .in1(JmpAddress[8]), .in2(1'b0), .in3(1'b0), .out(multiplexer_10_out),
    .sel({Reset, PCWrite}));
  D_Flip_Flop d_ff_9 (.clk(Clk), .D(multiplexer_9_out), .Q(Out[9]), .en(PC_Read));  // open: Qn, preset, reset
  D_Flip_Flop d_ff_10 (.clk(Clk), .D(multiplexer_10_out), .Q(Out[8]), .en(PC_Read));  // open: Qn, preset, reset
  Multiplexer #(.select(2), .enable("false")) multiplexer_11 (
    .in0(adder_1_out[7]), .in1(JmpAddress[7]), .in2(1'b0), .in3(1'b0), .out(multiplexer_11_out),
    .sel({Reset, PCWrite}));
  D_Flip_Flop d_ff_11 (.clk(Clk), .D(multiplexer_11_out), .Q(Out[7]), .en(PC_Read));  // open: Qn, preset, reset
  Multiplexer #(.select(2), .enable("false")) multiplexer_12 (
    .in0(adder_1_out[6]), .in1(JmpAddress[6]), .in2(1'b0), .in3(1'b0), .out(multiplexer_12_out),
    .sel({Reset, PCWrite}));
  Multiplexer #(.select(2), .enable("false")) multiplexer_13 (
    .in0(adder_1_out[5]), .in1(JmpAddress[5]), .in2(1'b0), .in3(1'b0), .out(multiplexer_13_out),
    .sel({Reset, PCWrite}));
  D_Flip_Flop d_ff_12 (.clk(Clk), .D(multiplexer_12_out), .Q(Out[6]), .en(PC_Read));  // open: Qn, preset, reset
  D_Flip_Flop d_ff_13 (.clk(Clk), .D(multiplexer_13_out), .Q(Out[5]), .en(PC_Read));  // open: Qn, preset, reset
  Multiplexer #(.select(2), .enable("false")) multiplexer_14 (
    .in0(adder_1_out[4]), .in1(JmpAddress[4]), .in2(1'b0), .in3(1'b0), .out(multiplexer_14_out),
    .sel({Reset, PCWrite}));
  Multiplexer #(.select(2), .enable("false")) multiplexer_15 (
    .in0(adder_1_out[3]), .in1(JmpAddress[3]), .in2(1'b0), .in3(1'b0), .out(multiplexer_15_out),
    .sel({Reset, PCWrite}));
  D_Flip_Flop d_ff_14 (.clk(Clk), .D(multiplexer_14_out), .Q(Out[4]), .en(PC_Read));  // open: Qn, preset, reset
  D_Flip_Flop d_ff_15 (.clk(Clk), .D(multiplexer_15_out), .Q(Out[3]), .en(PC_Read));  // open: Qn, preset, reset
  Multiplexer #(.select(2), .enable("false")) multiplexer_16 (
    .in0(adder_1_out[2]), .in1(JmpAddress[2]), .in2(1'b0), .in3(1'b0), .out(multiplexer_16_out),
    .sel({Reset, PCWrite}));
  D_Flip_Flop d_ff_16 (.clk(Clk), .D(multiplexer_16_out), .Q(Out[2]), .en(PC_Read));  // open: Qn, preset, reset
  Multiplexer #(.select(2), .enable("false")) multiplexer_17 (
    .in0(adder_1_out[1]), .in1(JmpAddress[1]), .in2(1'b0), .in3(1'b0), .out(multiplexer_17_out),
    .sel({Reset, PCWrite}));
  Multiplexer #(.select(2), .enable("false")) multiplexer_18 (
    .in0(adder_1_out[0]), .in1(JmpAddress[0]), .in2(1'b0), .in3(1'b0), .out(multiplexer_18_out),
    .sel({Reset, PCWrite}));
  D_Flip_Flop d_ff_17 (.clk(Clk), .D(multiplexer_17_out), .Q(Out[1]), .en(PC_Read));  // open: Qn, preset, reset
  D_Flip_Flop d_ff_18 (.clk(Clk), .D(multiplexer_18_out), .Q(Out[0]), .en(PC_Read));  // open: Qn, preset, reset
  Adder #(.width(20)) adder_1 (.a(20'h1), .b(Out), .out(adder_1_out), .cout(CarryOut));  // open: cin
endmodule

module Zero_Extender_10_bit (
  input  [9:0] \İnput ,
  output [19:0] ZeroExtended
);


  assign ZeroExtended = {{10{1'b0}}, \İnput };
endmodule

module Sign_Extender_14_bit (
  input  [13:0] \İnput ,
  output [17:0] SignExtended
);


  assign SignExtended = {{5{\İnput [13]}}, \İnput [12:0]};
endmodule

module Sign_Extender_6_bit (
  input  [5:0] \İnput ,
  output [17:0] SignExtended
);


  assign SignExtended = {{13{\İnput [5]}}, \İnput [4:0]};
endmodule

module Zero_Extender_3_bit (
  input  [2:0] \İnput ,
  output [17:0] ZeroExtended
);


  assign ZeroExtended = {{15{1'b0}}, \İnput };
endmodule

module Data_Memory (
  input  DataMem_Clear
);

  wire DataMem_Read, DatMem_Write, undriven;
  wire [19:0] ADDR, DataMem_Result, ram_1_data, SRC1;

  RAM #(.addrWidth(10), .dataWidth(20), .bus("separate")) ram_1 (
    .addr(ADDR[9:0]), .din(SRC1), .data(ram_1_data), .str(DatMem_Write), .clk(undriven), .ld(DataMem_Read),
    .clr(DataMem_Clear));  // open: sel
  Register #(.width(20)) register_1 (.D(ram_1_data), .Q(DataMem_Result), .clk(undriven));  // open: en, clr
  // Pins of 10 and 20 bits meet at ADDR
endmodule
